# Fritzing sketch AR02_2led.ino (saved by Fritzing 0.9.3b)
breadboards: 1

parts:
  LED1 = LED - 5mm [color="Red (633nm)" package="5 mm [THT]"]
  LED2 = LED - 5mm [color="Green (555nm)" package="5 mm [THT]"]
  R1 = Resistor [tolerance=±5% resistance=220 package=THT]
  R2 = Resistor [tolerance=±5% resistance=220 package=THT]
  부품1 = Arduino Uno (Rev3)

nets:
  N1: LED1.cathode, 부품1.D3_PWM
  N2: LED1.anode, R2.Pin_0
  N3: LED2.cathode, 부품1.D5_PWM
  N4: LED2.anode, R1.Pin_0
  N5: R1.Pin_1, R2.Pin_1, 부품1.GND
