# Fritzing sketch AR02_4digit.fzz (saved by Fritzing 0.9.3b)
breadboards: 1

parts:
  R1 = Resistor [tolerance=±5% resistance=330 package=THT]
  R2 = Resistor [tolerance=±5% resistance=330 package=THT]
  R3 = Resistor [tolerance=±5% resistance=330 package=THT]  # not connected
  R4 = Resistor [tolerance=±5% resistance=330 package=THT]
  R5 = Resistor [tolerance=±5% resistance=330 package=THT]
  R6 = Resistor [tolerance=±5% resistance=330 package=THT]
  R7 = Resistor [tolerance=±5% resistance=330 package=THT]
  R8 = Resistor [tolerance=±5% resistance=330 package=THT]
  부품1 = Arduino Uno (Rev3)
  U1 = 7-SEGMENT-4DIGIT [package=7-segment-4digit-5641]

nets:
  N1: R1.Pin_0, 부품1.D4
  N2: R1.Pin_1, U1.C
  N3: R2.Pin_0, 부품1.D3_PWM
  N4: R2.Pin_1, U1.B
  N5: R4.Pin_0, 부품1.D7
  N6: R4.Pin_1, U1.F
  N7: R5.Pin_0, 부품1.D8
  N8: R5.Pin_1, U1.G
  N9: R6.Pin_0, U1.DP
  N10: R6.Pin_1, 부품1.D9_PWM
  N11: R7.Pin_0, U1.A
  N12: R7.Pin_1, 부품1.D2
  N13: R8.Pin_0, U1.E
  N14: R8.Pin_1, 부품1.D6_PWM
  N15: 부품1.D10_PWM/SS, U1.DIG1
  N16: 부품1.D11_PWM/MOSI, U1.DIG2
  N17: 부품1.D12/MISO, U1.DIG3
  N18: 부품1.D13/SCK, U1.DIG4

custom parts:
  7-SEGMENT-4DIGIT: if you need make parts, send me e-mail and write. Price 1 part=0.9 WMZ (http://www.wmtransfer.com/) ~ 0.9 Euro
