# Fritzing sketch AR02_dm+module (saved by Fritzing 0.9.3b)
breadboards: 1

parts:
  8x8_LED_Modul_mit_MAX1 = 8x8 LED Modul mit MAX7219 [package=THT]
  부품1 = Arduino Uno (Rev3)

nets:
  N1: 8x8_LED_Modul_mit_MAX1.VCC_Eingang, 부품1.5V
  N2: 8x8_LED_Modul_mit_MAX1.GND_Eingang, 부품1.GND
  N3: 8x8_LED_Modul_mit_MAX1.DIN_Eingang, 부품1.D4
  N4: 8x8_LED_Modul_mit_MAX1.CS_Eingang, 부품1.D2
  N5: 8x8_LED_Modul_mit_MAX1.CLK_Eingang, 부품1.D3_PWM
